# Fritzing sketch Maleficent_dress (saved by Fritzing 0.9.2b)

parts:
  FLORA1 = Adafruit_Flora
  strip_DX = Neopixel Strip -- White (30/m)
  strip_SX = Neopixel Strip -- White (30/m)
  VCC1 = 4 x AAA Battery Mount
  S1 = Pushbutton [package="[THT]"]
  R1 = Resistor [tolerance=±5% resistance=100k package="0805 [SMD]"]
  J1 = female pin header, 3 pins [form="♀ (female)"]
  J2 = male pin header, 3 pins [form="♂ (male)"]

nets:
  N1: FLORA1.connector1, VCC1.-, R1.Pin_0
  N2: FLORA1.connector7, strip_SX.GND
  N3: FLORA1.connector10, strip_SX.Din, J1.pin2
  N4: FLORA1.connector11, J1.pin3
  N5: FLORA1.connector12, S1.Pin_1, S1.Pin_2, R1.Pin_1
  N6: FLORA1.connector14, S1.Pin_4
  N7: strip_DX.GND, J2.pin3
  N8: strip_DX.Din, J2.pin2
  N9: strip_DX.+5V, J2.pin1
  N10: strip_SX.+5V, VCC1.+, J1.pin1

custom parts:
  Neopixel Strip -- White (30/m): These NeoPixel strips have 30 digitally-addressable pixel LEDs per meter and are very affordable and are only 12.5 mm wide, 10 mm if you remove the strip from the casing.
